# Fritzing sketch simon_says (saved by Fritzing 0.9.9b)
circuit board: 8.46667cm x 5.64444cm
breadboards: 1

parts:
  Part1 = Arduino Nano (Rev3.0)
  R1 = Resistor [tolerance=±5% power=0.25 resistance=10k package=THT]
  R2 = Resistor [tolerance=±5% power=0.25 resistance=10k package=THT]
  R3 = Resistor [tolerance=±5% power=0.25 resistance=10k package=THT]
  R4 = Resistor [tolerance=±5% power=0.25 resistance=10k package=THT]
  LED1 = LED - 5mm [color="Yellow (595nm)" current=0.030 package="5 mm [THT]"]
  R6 = Resistor [tolerance=±5% power=0.25 resistance=330 package=THT]
  S1 = Pushbutton [package="[THT]"]
  R7 = Resistor [tolerance=±5% power=0.25 resistance=510 package=THT]
  S2 = Pushbutton [package="[THT]"]
  R8 = Resistor [tolerance=±5% power=0.25 resistance=510 package=THT]
  S3 = Pushbutton [package="[THT]"]
  R9 = Resistor [tolerance=±5% power=0.25 resistance=330 package=THT]
  S4 = Pushbutton [package="[THT]"]
  LED2 = LED - 5mm [color="Blue (430nm)" current=0.030 package="5 mm [THT]"]
  LED3 = LED - 5mm [color="Green (555nm)" current=0.030 package="5 mm [THT]"]
  LED4 = LED - 5mm [color="Red (635nm)" current=0.030 package="5 mm [THT]"]

nets:
  N1: Part1.GND, R1.Pin_0, R2.Pin_0, R3.Pin_0, R4.Pin_0, R7.Pin_0, R8.Pin_0, R9.Pin_0
  N2: Part1.D5, Part1.D6, R4.Pin_1, LED1.anode, S1.Pin_1, S1.Pin_2
  N3: Part1.D7, Part1.D10, R2.Pin_1, S2.Pin_1, S2.Pin_2, LED2.anode
  N4: Part1.D8, Part1.D11/MOSI, R3.Pin_1, S3.Pin_1, S3.Pin_2, LED3.anode
  N5: Part1.D9, Part1.D12/MISO, R1.Pin_1, S4.Pin_1, S4.Pin_2, LED4.anode
  N6: Part1.5V, S1.Pin_3, S1.Pin_4, S2.Pin_3, S2.Pin_4, S3.Pin_3, S3.Pin_4, S4.Pin_3, S4.Pin_4
  N7: LED1.cathode, R6.Pin_1
  N8: R7.Pin_1, LED2.cathode
  N9: R8.Pin_1, LED3.cathode
  N10: R9.Pin_1, LED4.cathode

notes:
  Wire connections with output pins:
  {R,G,B,Y} LEDs connect to {9,8,7,6}.
  Wire connections with input pins:
  {R,G,B,Y} buttons connect to {12,11,10,5}.
